# Fritzing sketch LED Matrix (saved by Fritzing 0.9.10b)
perfboards: 1

parts:
  Part1 = Arduino Nano (Rev3.0)
  J1 = Power Jack [package=power_jack_pth_lock]
  R3 = Rotary Potentiometer (Small) [maximum_resistance=100kΩ knob_status=50% power=0.5W package=THT]
  R4 = Rotary Potentiometer (Small) [maximum_resistance=100kΩ knob_status=50% power=0.5W package=THT]
  S1 = Pushbutton [package="[THT]"]
  S2 = Pushbutton [package="[THT]"]

nets:
  GND: Part1.GND, J1.GND, R3.leg1, R4.leg1, S1.Pin_1, S1.Pin_2, S2.Pin_1, S2.Pin_2
  N1: Part1.D6, S1.Pin_3, S1.Pin_4
  N2: Part1.D7, S2.Pin_3, S2.Pin_4
  N3: Part1.VIN, J1.PWR
  N4: Part1.5V, R3.leg2, R4.leg2
  N5: Part1.A2, R4.wiper
  N6: Part1.A1, R3.wiper
